# Fritzing sketch arduino waterer breadboard (saved by Fritzing 0.9.0b)
circuit board: 8.46667cm x 5.64444cm
breadboards: 1

parts:
  Q2 = Basic FET P-Channel [package="TO220 [THT]"]
  LED1 = RGB LED (com. cathode, rgb) [package="5 mm [THT]"]
  R1 = Resistor [tolerance=±5% resistance=220 package=THT]
  R2 = Resistor [tolerance=±5% resistance=220 package=THT]
  R3 = Resistor [tolerance=±5% resistance=220 package=THT]
  R4 = Rotary Potentiometer (Small) [maximum_resistance=100kΩ package=THT]
  S1 = Pushbutton [package="[THT]"]
  U1 = Humdity Sensor [package=sht1x]
  L1 = Solenoid
  Part2 = Arduino Nano (Rev3.0)
  J1 = Power Jack [package=power_jack_combo]

nets:
  N1: Q2.gate, Part2.D2
  GND: Q2.drain, LED1.common_cathode, R4.leg1, S1.Pin_1, S1.Pin_2, U1.GND, Part2.GND, J1.GND
  N2: Q2.source, S1.Pin_3, S1.Pin_4, L1.pin2
  N3: LED1.red_anode, R1.Pin_0
  N4: LED1.green_anode, R2.Pin_0
  N5: LED1.blue_anode, R3.Pin_0
  N6: R1.Pin_1, Part2.D6
  N7: R2.Pin_1, Part2.D5
  N8: R3.Pin_1, Part2.D3
  N9: R4.wiper, Part2.A4
  VCC: R4.leg2, U1.VCC, Part2.5V
  N10: U1.A0, Part2.A5
  N11: U1.D0, Part2.D1/TX
  N12: L1.pin1, Part2.VIN, J1.PWR
