# Fritzing sketch arduino waterer nano minimal pcb (saved by Fritzing 0.9.2b)
circuit board: 5.95cm x 6.7cm
perfboards: 1

parts:
  R5 = Resistor [tolerance=±5% resistance=220 package=THT]
  R6 = Resistor [tolerance=±5% resistance=220 package=THT]
  R7 = Resistor [tolerance=±5% resistance=220 package=THT]
  Q3 = Basic FET P-Channel [package="TO220 [THT]"]
  R8 = Rotary Potentiometer (Large) [maximum_resistance=100kΩ package=THT]
  J2 = Power Jack [package=power_jack_slot]
  J3 = female pin header, 4 pins [form="♀ (female)"]
  J4 = female pin header, 4 pins [form="♀ (female)"]
  J5 = female pin header, 2 pins [form="♀ (female)"]
  J6 = female pin header, 2 pins [form="♀ (female)"]
  J7 = female pin header, 4 pins [form="♀ (female)"]
  J8 = female pin header, 2 pins [form="♀ (female)"]
  J9 = female pin header, 9 pins [form="♀ (female)"]

nets:
  N1: R5.Pin_0, J9.pin1
  N2: R5.Pin_1, J4.pin1
  N3: R6.Pin_0, J9.pin2
  N4: R6.Pin_1, J4.pin3
  N5: R7.Pin_0, J9.pin4
  N6: R7.Pin_1, J4.pin4
  N7: Q3.gate, J9.pin5
  N8: Q3.drain, J5.pin1, J6.pin1
  N9: Q3.source, R8.leg1, J2.GNDBREAK, J3.pin4, J4.pin2, J7.pin3
  N10: R8.wiper, J8.pin1
  N11: J2.PWR, J5.pin2, J6.pin2, J7.pin4
  N12: J3.pin1, J8.pin2
  N13: J3.pin2, J9.pin9
  N14: J3.pin3, J7.pin1
