# Fritzing sketch arduino waterer nano pcb (saved by Fritzing 0.9.2b)
circuit board: 5.92cm x 6.7cm
perfboards: 1

parts:
  Part3 = Arduino Nano (Rev3.0)
  R5 = Resistor [tolerance=±5% resistance=220 package=THT]
  R6 = Resistor [tolerance=±5% resistance=220 package=THT]
  R7 = Resistor [tolerance=±5% resistance=220 package=THT]
  Q3 = Basic FET P-Channel [package="TO220 [THT]"]
  R8 = Rotary Potentiometer (Large) [maximum_resistance=100kΩ package=THT]
  J2 = Power Jack [package=power_jack_slot]
  J3 = female pin header, 4 pins [form="♀ (female)"]
  J4 = female pin header, 4 pins [form="♀ (female)"]
  J5 = female pin header, 2 pins [form="♀ (female)"]
  J6 = female pin header, 2 pins [form="♀ (female)"]

nets:
  N1: Part3.D1/TX, J3.pin2
  N2: Part3.GND, Q3.source, R8.leg1, J2.GNDBREAK, J3.pin4, J4.pin2
  N3: Part3.D2, Q3.gate
  N4: Part3.D3, R7.Pin_0
  N5: Part3.D5, R6.Pin_0
  N6: Part3.D6, R5.Pin_0
  N7: Part3.VIN, J2.PWR, J5.pin2, J6.pin2
  N8: Part3.5V, J3.pin3
  N9: Part3.A5, J3.pin1
  N10: Part3.A4, R8.wiper
  N11: R5.Pin_1, J4.pin1
  N12: R6.Pin_1, J4.pin3
  N13: R7.Pin_1, J4.pin4
  N14: Q3.drain, J5.pin1, J6.pin1
