# Fritzing sketch arduino waterer uno breadboard (saved by Fritzing 0.9.0b)
circuit board: 8.46667cm x 5.64444cm
breadboards: 1

parts:
  Part1 = Arduino Uno (Rev3)
  Q2 = Basic FET P-Channel [package="TO220 [THT]"]
  LED1 = RGB LED (com. cathode, rgb) [package="5 mm [THT]"]
  R1 = Resistor [tolerance=±5% resistance=220 package=THT]
  R2 = Resistor [tolerance=±5% resistance=220 package=THT]
  R3 = Resistor [tolerance=±5% resistance=220 package=THT]
  R4 = Rotary Potentiometer (Small) [maximum_resistance=100kΩ package=THT]
  S1 = Pushbutton [package="[THT]"]
  U1 = Humdity Sensor [package=sht1x]
  L1 = Solenoid
  J1 = Power Jack [package=power_jack_combo]

nets:
  N1: Part1.A4/SDA, R4.wiper
  N2: Part1.A5/SCL, U1.A0
  N3: Part1.D1/TX, U1.D0
  N4: Part1.D2, Q2.gate
  N5: Part1.D3_PWM, R3.Pin_1
  N6: Part1.D5_PWM, R2.Pin_1
  N7: Part1.D6_PWM, R1.Pin_1
  5V: Part1.5V, R4.leg2, U1.VCC
  GND: Part1.GND, LED1.common_cathode, R4.leg1, U1.GND
  N8: Q2.drain, S1.Pin_1, S1.Pin_2, J1.GND
  N9: Q2.source, S1.Pin_3, S1.Pin_4, L1.pin2
  N10: LED1.red_anode, R1.Pin_0
  N11: LED1.green_anode, R2.Pin_0
  N12: LED1.blue_anode, R3.Pin_0
  N13: L1.pin1, J1.PWR
